// Logisim project decodificador7seg.circ as structural Verilog
module sevenseg (
  input  S3,
  input  S2,
  input  S1,
  input  S0,
  output HEX00,
  output HEX01,
  output HEX02,
  output HEX03,
  output HEX04,
  output HEX05,
  output HEX06
);

  wire and_1_out, and_2_out, and_3_out, and_4_out, and_5_out, and_6_out, and_7_out, and_8_out, and_9_out,
       and_10_out, and_11_out, and_12_out, and_13_out, and_14_out, and_16_out, and_17_out, not_1_out,
       not_2_out, not_3_out, not_4_out;

  not not_1 (not_1_out, S3);
  not not_2 (not_2_out, S2);
  not not_3 (not_3_out, S1);
  not not_4 (not_4_out, S0);
  and and_1 (and_1_out, not_1_out, not_2_out, not_3_out, S0);
  and and_2 (and_2_out, not_1_out, S2, not_3_out, not_4_out);
  and and_3 (and_3_out, not_1_out, not_3_out, S0);
  and and_4 (and_4_out, S3, S2, not_3_out, not_4_out);
  and and_5 (and_5_out, not_1_out, not_2_out, not_3_out, S0);
  and and_6 (and_6_out, not_1_out, not_2_out, S1, not_4_out);
  and and_7 (and_7_out, S3, S2, not_3_out, not_4_out);
  and and_8 (and_8_out, S3, S2, S1, S0);
  and and_9 (and_9_out, not_1_out, not_2_out, not_3_out, S0);
  and and_10 (and_10_out, not_1_out, S2, not_3_out, not_4_out);
  and and_11 (and_11_out, S3, not_2_out, S1, not_4_out);
  and and_12 (and_12_out, S3, S2, S1, S0);
  and and_13 (and_13_out, not_1_out, not_2_out, S1, S0);
  and and_14 (and_14_out, not_1_out, S2, not_3_out);
  and and_15 (HEX05, not_1_out, not_2_out, S1);
  and and_16 (and_16_out, not_1_out, not_2_out, not_3_out);
  and and_17 (and_17_out, S3, S2, not_3_out, not_4_out);
  or or_1 (HEX00, and_1_out, and_2_out);
  or or_2 (HEX01, and_3_out, and_4_out);
  or or_3 (HEX02, and_5_out, and_6_out, and_7_out, and_8_out);
  or or_4 (HEX03, and_9_out, and_10_out, and_11_out, and_12_out);
  or or_5 (HEX04, and_13_out, and_14_out);
  or or_6 (HEX06, and_16_out, and_17_out);
  _7_Segment_Display #(.active("false")) a (
    .g(HEX06), .f(HEX05), .a(HEX00), .b(HEX01), .e(HEX04), .d(HEX03), .c(HEX02));  // open: dp
endmodule
