// Logisim project meta2cd.circ as structural Verilog: 1 circuit, main circuit main
module main (
  input  A,
  input  B,
  input  C,
  input  D,
  input  E,
  output S
);

  wire and_1_out, and_2_out, nor_1_out;

  and and_1 (and_1_out, A, B);
  nor nor_1 (nor_1_out, and_1_out, C);
  and and_2 (and_2_out, nor_1_out, D);
  or or_1 (S, and_2_out, E);
endmodule
