// Logisim project modomanutencao.circ as structural Verilog: 1 circuit, main circuit main
module main (
  input  F,
  input  T,
  input  P,
  input  L,
  output [3:0] S
);


  assign S = 4'b0110;
endmodule
