// Logisim project modonormal.circ as structural Verilog: 1 circuit, main circuit main
module main (
  input  F,
  input  T,
  input  P,
  input  L,
  output [3:0] S
);

  wire a0_out, a1_out, a2_out, a3_out, a4_out, a5_out, a6_out, a7_out, a8_out, a9_out, a10_out, a11_out,
       not_1_out, not_2_out, not_3_out;

  not not_1 (not_1_out, F);
  not not_2 (not_2_out, P);
  not not_3 (not_3_out, L);
  and a0 (a0_out, F, P, not_3_out);
  and a1 (a1_out, F, T);
  and a2 (a2_out, P, not_3_out);
  and a3 (a3_out, F, T, P);
  and a4 (a4_out, T, not_2_out);
  and a5 (a5_out, T, L);
  and a6 (a6_out, F, not_2_out);
  and a7 (a7_out, F, L);
  and a8 (a8_out, F, T);
  and a9 (a9_out, not_1_out, not_2_out, not_3_out);
  and a10 (a10_out, not_1_out, T);
  and a11 (a11_out, T, P);
  or o0 (S[3], a0_out, a1_out);
  or o1 (S[2], a2_out, a3_out);
  or o2 (S[1], a4_out, a5_out, a6_out, a7_out, a8_out);
  or o3 (S[0], a9_out, a10_out, a11_out);

  // Notes on the sheet:
  //   nF
  //   nP
  //   nL
  //   w0
  //   w1
  //   w2
  //   w3
  //   w4
  //   w5
  //   w6
  //   w7
  //   w8
  //   w9
  //   w10
  //   w11
  //   w12
  //   w13
  //   w14
  //   w15
endmodule
