// Logisim project normalsimplificado.circ as structural Verilog
module normalsimples (
  input  F,
  input  T,
  input  P,
  input  L,
  output [3:0] S
);

  wire and_1_out, and_2_out, and_3_out, and_4_out, and_5_out, not_1_out, not_2_out, or_1_out, or_2_out,
       or_3_out, or_4_out, or_5_out, or_6_out;

  not not_1 (not_1_out, P);
  not not_2 (not_2_out, L);
  and and_1 (and_1_out, P, not_2_out);
  or or_1 (or_1_out, T, F);
  or or_2 (or_2_out, T, F);
  and and_2 (and_2_out, T, F, not_1_out);
  and and_3 (and_3_out, T, F, L);
  or or_3 (or_3_out, not_2_out, F);
  or or_4 (or_4_out, and_1_out, T);
  and and_4 (and_4_out, not_1_out, or_1_out);
  and and_5 (and_5_out, L, or_2_out);
  or or_5 (or_5_out, and_2_out, and_3_out, F);
  and and_6 (S[0], or_3_out, T, P);
  and and_7 (S[3], F, or_4_out);
  or or_6 (or_6_out, and_4_out, and_5_out, F);
  and and_8 (S[2], or_6_out, T);
  and and_9 (S[1], or_5_out, T);
endmodule
