// Logisim project total.circ as structural Verilog: 1 circuit, main circuit main
module main (
  input  M1,
  input  M0,
  input  F,
  input  T,
  input  P,
  input  L,
  output [3:0] S
);

  wire and_1_out, and_2_out, and_3_out, and_4_out, and_5_out, and_6_out, and_7_out, and_8_out, and_9_out,
       and_10_out, and_11_out, and_12_out, and_13_out, and_14_out, and_15_out, not_1_out, not_2_out,
       not_3_out, not_4_out, not_5_out;

  not not_1 (not_1_out, M1);
  not not_2 (not_2_out, F);
  not not_3 (not_3_out, T);
  not not_4 (not_4_out, P);
  not not_5 (not_5_out, L);
  and and_1 (and_1_out, M1, M0);
  and and_2 (and_2_out, not_1_out, F, not_5_out);
  and and_3 (and_3_out, not_1_out, F, T);
  and and_4 (and_4_out, P, not_5_out);
  and and_5 (and_5_out, F, not_3_out, not_5_out);
  and and_6 (and_6_out, F, T, P);
  and and_7 (and_7_out, T, not_4_out);
  and and_8 (and_8_out, T, L);
  and and_9 (and_9_out, F, L);
  and and_10 (and_10_out, F, T);
  and and_11 (and_11_out, not_1_out, not_2_out, not_4_out, not_5_out);
  and and_12 (and_12_out, not_1_out, not_2_out, T);
  and and_13 (and_13_out, not_1_out, T, P, L);
  and and_14 (and_14_out, M0, T, P);
  and and_15 (and_15_out, M1, M0);
  or or_1 (S[3], and_1_out, and_2_out, and_3_out);
  or or_2 (S[2], and_4_out, and_5_out, and_6_out, M1);
  or or_3 (S[1], and_7_out, and_8_out, and_9_out, and_10_out, M1);
  or or_4 (S[0], and_11_out, and_12_out, and_13_out, and_14_out, and_15_out);
endmodule
